# Fritzing sketch main (saved by Fritzing 0.9.3b)
perfboards: 1

parts:
  U1 = ATTINY13 [package=dip]
  Q1 = NPN-Transistor [package="TO92 [THT]"]
  Q3 = NPN-Transistor [package="TO92 [THT]"]
  C1 = Ceramic Capacitor [capacitance="100 nF" package="0805 [SMD, multilayer]"]
  C3 = Electrolytic Capacitor [package="2cm H-Type"]
  C4 = Electrolytic Capacitor [package="2cm H-Type"]
  R1 = Resistor [tolerance=±5% resistance=510 package="0805 [SMD]"]
  J1 = Dagu DGServo 9g header (male) [package=THT]
  M1 = DC Motor
  IC1 = Voltage Regulator [package=to-92]
  Part1 = Soil Moisture Sensor
  Solar_Cell1 = 5V 100mA Polycrystalline PET Solar Cell [part_number=IM130407002]  # not connected
  Part2 = Power Cell LiPo Charger/Booster
  R8 = Resistor [tolerance=±1% resistance=10 package="2512 [SMD]"]
  USBTTL1 = USB TTL Serial Cable
  BAT1 = Battery Holders [package=lipo-1100mAh]
  R7 = Resistor [tolerance=±1% resistance=10k package="0805 [SMD]"]  # not connected
  R2 = Resistor [tolerance=±5% resistance=3.3k package="0805 [SMD]"]

nets:
  N1: U1.PB3(ADC3), J1.gnd, USBTTL1.RX
  N2: U1.PB4(ADC2), J1.Vcc
  N3: U1.PB0(MOSI), R1.Pin_0
  N4: U1.PB1(MISO), Part1.VCC
  N5: U1.PB2(SCK_ADC1), R2.Pin_1
  VCC: U1.VCC, C1.0, Part2.VCC, Part2.PS, BAT1.+
  N6: Q1.B, R2.Pin_0
  N7: Q1.C, IC1.IN
  N8: Q3.B, R1.Pin_1, R8.Pin_1
  N9: Q3.C, M1.pin_2
  N10: C3.-, C4.-
  N11: C4.+, IC1.GND
  N12: J1.pulse, USBTTL1.GND
  N13: IC1.OUT, Part2.5VIN
  N14: Part2.GND, BAT1.-

notes:
  TX
  78l05
  5V
  104
  USB Serial
  Pump DC Motor
  Moisture Sensor
  A0
  Lithium-ion Battery
  Lithium-ion Charger with Protection
  NPN
  510R
  10K
  3.3K

custom parts:
  5V 100mA Polycrystalline PET Solar Cell: This is 5V 100mA Polycrystalline PET Solar Cell. It is high quality and exquisite appearance. It is used in all kinds of high-grade electronic products.
